// Logisim project computer_beta.circ as structural Verilog: 2 circuits, main circuit ComputerNew
module ComputerNew (
  output [15:0] out_1,
  output [15:0] out_2,
  output [15:0] out_3,
  output [15:0] out_4,
  output [15:0] out_5,
  output [15:0] out_6,
  output [15:0] out_7,
  output [15:0] out_8,
  output [15:0] out_9,
  output [15:0] out_10,
  output [15:0] out_11,
  output [15:0] out_12,
  output [15:0] out_13,
  output [15:0] out_14,
  output [15:0] out_15,
  output [15:0] out_16,
  output [15:0] out_17,
  output [15:0] out_18
);

  wire adder_2_cout, and_1_out, and_2_out, and_3_out, and_4_out, and_5_out, and_6_out, and_7_out, and_8_out,
       and_9_out, and_10_out, and_11_out, and_12_out, and_13_out, and_14_out, and_15_out, and_16_out,
       and_17_out, and_18_out, and_19_out, and_21_out, and_22_out, and_23_out, and_24_out, and_25_out,
       and_26_out, and_27_out, and_28_out, and_29_out, and_30_out, and_31_out, and_32_out, and_33_out,
       and_34_out, and_35_out, and_36_out, and_37_out, and_38_out, and_39_out, and_40_out, and_41_out,
       and_42_out, and_43_out, Clock_0_out, comparator_2_eq, comparator_3_eq, demultiplexer_1_out0,
       demultiplexer_1_out1, demultiplexer_1_out2, demultiplexer_1_out3, demultiplexer_1_out4,
       demultiplexer_1_out5, demultiplexer_1_out6, demultiplexer_1_out7, demultiplexer_2_out0,
       demultiplexer_2_out1, multiplexer_1_out, nand_1_out, nand_3_out, nor_1_out, nor_2_out, nor_3_out,
       nor_4_out, not_1_out, not_2_out, not_3_out, not_4_out, not_5_out, not_6_out, not_7_out, not_8_out,
       not_9_out, not_10_out, not_11_out, not_12_out, not_13_out, not_14_out, not_15_out, not_16_out,
       not_17_out, not_18_out, not_19_out, not_20_out, not_21_out, not_22_out, not_23_out, not_24_out,
       not_25_out, not_26_out, not_27_out, not_28_out, not_29_out, not_30_out, not_31_out, not_32_out,
       not_33_out, not_34_out, not_35_out, not_36_out, not_37_out, not_38_out, not_39_out, not_40_out,
       not_41_out, not_42_out, not_43_out, not_44_out, not_45_out, not_46_out, not_47_out, not_48_out,
       not_49_out, not_50_out, not_51_out, or_1_out, or_2_out, or_3_out, or_4_out, or_5_out, or_6_out,
       or_7_out, or_8_out, or_9_out, or_12_out, or_13_out, or_14_out, or_15_out, or_16_out, or_17_out,
       pull_resistor_2_node, pull_resistor_3_node, pull_resistor_4_node, RESET_qn, subtractor_1_bout,
       t_ff_1_q, xor_1_out;
  wire [0:0] keyboard_1_avail;
  wire [2:0] multiplexer_6_out;
  wire [3:0] controlled_buffer_6_out;
  wire [4:0] FLAGS_q, or_11_out;
  wire [6:0] keyboard_1_data;
  wire [11:0] multiplexer_9_out, subtractor_2_out;
  wire [14:0] multiplexer_13_out;
  wire [15:0] adder_1_out, adder_2_out, and_20_out, bitfinder_1_index, controlled_buffer_1_out,
       controlled_buffer_5_out, controlled_buffer_7_out, divider_1_out, divider_1_rem, MEMORY_dout,
       multiplexer_2_out, multiplexer_3_out, multiplexer_4_out, multiplexer_5_out, multiplexer_7_out,
       multiplexer_8_out, multiplexer_10_out, multiplexer_11_out, multiplexer_12_out, multiplier_1_out,
       or_10_out, PROGRAM_data, shifter_1_out, shifter_2_out, shifter_3_out, shifter_4_out, subtractor_1_out,
       SYSTEM_data;
  wire [15:12] multiplexer_9_out_2;
  wire [15:15] multiplexer_13_out_2;

  Clock Clock_0 (.out(Clock_0_out));
  not not_1 (not_1_out, Clock_0_out);
  J_K_Flip_Flop #(.trigger("falling")) RESET (
    .J(1'b1), .K(1'b0), .clk(Clock_0_out), .Qn(RESET_qn));  // open: Q, preset, reset
  Register #(.width(5)) FLAGS (.D(or_11_out), .en(or_1_out), .clk(Clock_0_out), .Q(FLAGS_q), .clr(RESET_qn));
  Register #(.trigger("low"), .width(16)) IR (
    .D(controlled_buffer_1_out), .en(not_1_out), .clk(Clock_0_out), .Q(out_14), .clr(RESET_qn));
  Multiplexer #(.select(3)) multiplexer_1 (
    .in0(1'b1), .in1(FLAGS_q[0]), .in2(FLAGS_q[1]), .in3(FLAGS_q[2]), .in4(FLAGS_q[3]), .in5(FLAGS_q[4]),
    .in6(1'b1), .in7(1'b1), .out(multiplexer_1_out), .sel(out_14[9:7]));
  not not_2 (not_2_out, out_14[0]);
  not not_3 (not_3_out, out_14[1]);
  not not_4 (not_4_out, out_14[3]);
  not not_5 (not_5_out, out_14[1]);
  not not_6 (not_6_out, out_14[3]);
  not not_7 (not_7_out, out_14[2]);
  not not_8 (not_8_out, out_14[3]);
  not not_9 (not_9_out, out_14[0]);
  not not_10 (not_10_out, out_14[2]);
  not not_11 (not_11_out, out_14[3]);
  not not_12 (not_12_out, out_14[1]);
  not not_13 (not_13_out, out_14[2]);
  not not_14 (not_14_out, out_14[3]);
  not not_15 (not_15_out, out_14[0]);
  not not_16 (not_16_out, out_14[1]);
  not not_17 (not_17_out, out_14[2]);
  not not_18 (not_18_out, out_14[3]);
  not not_19 (not_19_out, out_14[0]);
  not not_20 (not_20_out, out_14[3]);
  not not_21 (not_21_out, out_14[0]);
  not not_22 (not_22_out, out_14[0]);
  not not_23 (not_23_out, out_14[1]);
  not not_24 (not_24_out, out_14[2]);
  and and_1 (and_1_out, not_2_out, not_3_out, out_14[2], not_4_out);
  and and_2 (and_2_out, out_14[0], not_5_out, out_14[2], not_6_out);
  and and_3 (and_3_out, out_14[0], out_14[1], not_7_out, not_8_out);
  and and_4 (and_4_out, not_9_out, out_14[1], not_10_out, not_11_out);
  and and_5 (and_5_out, out_14[0], not_12_out, not_13_out, not_14_out);
  and and_6 (and_6_out, not_15_out, not_16_out, not_17_out, not_18_out);
  and and_7 (and_7_out, not_19_out, out_14[1], out_14[2], not_20_out);
  and and_8 (and_8_out, not_21_out, out_14[1], out_14[2], out_14[3]);
  and and_9 (and_9_out, not_22_out, not_23_out, not_24_out, out_14[3]);
  or or_1 (or_1_out, and_1_out, and_2_out);
  and and_10 (and_10_out, and_3_out, multiplexer_1_out);
  and and_11 (and_11_out, and_5_out, multiplexer_1_out);
  and and_12 (and_12_out, and_6_out, multiplexer_1_out);
  and and_13 (and_13_out, and_7_out, multiplexer_1_out);
  or or_2 (or_2_out, and_9_out, and_8_out);
  or or_3 (or_3_out, and_13_out, and_1_out, and_2_out, and_8_out, and_9_out, and_4_out, and_11_out, and_12_out);
  or or_4 (or_4_out, and_2_out, or_2_out, and_1_out);
  or or_5 (or_5_out, and_13_out, and_11_out);
  or or_6 (or_6_out, or_5_out, not_1_out);
  Demultiplexer #(.select(3)) demultiplexer_1 (
    .out0(demultiplexer_1_out0), .out1(demultiplexer_1_out1), .out2(demultiplexer_1_out2),
    .out3(demultiplexer_1_out3), .out4(demultiplexer_1_out4), .out5(demultiplexer_1_out5),
    .out6(demultiplexer_1_out6), .out7(demultiplexer_1_out7), .in(or_3_out), .sel(out_14[6:4]));
  Register #(.trigger("falling"), .width(16)) R0 (
    .D(controlled_buffer_1_out), .en(demultiplexer_1_out0), .clk(Clock_0_out), .Q(out_1), .clr(RESET_qn));
  Register #(.trigger("falling"), .width(16)) R4 (
    .D(controlled_buffer_1_out), .en(demultiplexer_1_out4), .clk(Clock_0_out), .Q(out_17), .clr(RESET_qn));
  Register #(.trigger("falling"), .width(16)) R1 (
    .D(controlled_buffer_1_out), .en(demultiplexer_1_out1), .clk(Clock_0_out), .Q(out_5), .clr(RESET_qn));
  Register #(.trigger("falling"), .width(16)) R5 (
    .D(controlled_buffer_1_out), .en(demultiplexer_1_out5), .clk(Clock_0_out), .Q(out_2), .clr(RESET_qn));
  Register #(.trigger("falling"), .width(16)) R2 (
    .D(controlled_buffer_1_out), .en(demultiplexer_1_out2), .clk(Clock_0_out), .Q(out_9), .clr(RESET_qn));
  Register #(.trigger("falling"), .width(16)) SP (
    .D(controlled_buffer_1_out), .en(demultiplexer_1_out6), .clk(Clock_0_out), .Q(out_6), .clr(RESET_qn));
  Register #(.trigger("falling"), .width(16)) R3 (
    .D(controlled_buffer_1_out), .en(demultiplexer_1_out3), .clk(Clock_0_out), .Q(out_13), .clr(RESET_qn));
  Multiplexer #(.width(16)) multiplexer_2 (
    .in0(adder_1_out), .in1(controlled_buffer_1_out), .out(multiplexer_2_out), .sel(demultiplexer_1_out7));
  or or_7 (or_7_out, demultiplexer_1_out7, Clock_0_out);
  nand nand_1 (nand_1_out, or_7_out, and_41_out);
  Register #(.trigger("falling"), .width(16)) PC (
    .D(multiplexer_2_out), .en(nand_1_out), .clk(Clock_0_out), .Q(out_10), .clr(RESET_qn));
  and and_14 (and_14_out, not_25_out, and_13_out);
  not not_25 (not_25_out, Clock_0_out);
  Adder #(.width(16)) adder_1 (.a(out_10), .b(multiplexer_3_out), .out(adder_1_out));  // open: cin, cout
  Multiplexer #(.width(16)) multiplexer_3 (.in0(16'h1), .in1(16'h2), .out(multiplexer_3_out), .sel(and_14_out));
  Multiplexer #(.width(16)) multiplexer_4 (.in0(out_10), .in1(adder_1_out), .out(multiplexer_4_out), .sel(and_15_out));
  and and_15 (and_15_out, Clock_0_out, and_13_out);
  Multiplexer #(.width(16)) multiplexer_5 (
    .in0(multiplexer_4_out), .in1(16'h3bf), .out(multiplexer_5_out), .sel(and_41_out));
  Multiplexer #(.width(3)) multiplexer_6 (.in0(out_14[15:13]), .in1(3'b111), .out(multiplexer_6_out), .sel(or_8_out));
  or or_8 (or_8_out, and_13_out, not_1_out);
  Multiplexer #(.select(3), .width(16)) multiplexer_7 (
    .in0(out_1), .in1(out_5), .in2(out_9), .in3(out_13), .in4(out_17), .in5(out_2), .in6(out_6),
    .in7(multiplexer_5_out), .out(multiplexer_7_out), .sel(out_14[12:10]));
  Multiplexer #(.select(3), .width(16)) multiplexer_8 (
    .in0(out_1), .in1(out_5), .in2(out_9), .in3(out_13), .in4(out_17), .in5(out_2), .in6(out_6),
    .in7(multiplexer_5_out), .out(multiplexer_8_out), .sel(multiplexer_6_out));
  Multiplexer #(.select(3), .width(16)) multiplexer_9 (
    .in0(out_1), .in1(out_5), .in2(out_9), .in3(out_13), .in4(out_17), .in5(out_2), .in6(out_6),
    .in7(multiplexer_5_out), .out({multiplexer_9_out_2, multiplexer_9_out}), .sel(multiplexer_6_out));
  assign controlled_buffer_1_out = and_16_out ? multiplexer_7_out : 16'bz;  // Controlled_Buffer controlled_buffer_1
  and and_16 (and_16_out, Clock_0_out, and_10_out);
  assign controlled_buffer_1_out = and_17_out ? multiplexer_8_out : 16'bz;  // Controlled_Buffer controlled_buffer_2
  and and_17 (and_17_out, Clock_0_out, and_12_out);
  and and_18 (and_18_out, Clock_0_out, and_4_out);
  assign controlled_buffer_1_out = and_18_out ? {{7{1'b0}}, out_14[15:7]} : 16'bz;  // Controlled_Buffer controlled_buffer_3
  and and_19 (and_19_out, Clock_0_out, or_9_out);
  or or_9 (or_9_out, and_2_out, or_4_out);
  Multiplexer #(.width(16)) multiplexer_10 (
    .in0(multiplexer_8_out), .in1({{7{1'b0}}, out_14[15:7]}), .out(multiplexer_10_out), .sel(or_2_out));
  xor xor_1 (xor_1_out, multiplexer_10_out[15], multiplexer_7_out[15]);
  not not_26 (not_26_out, xor_1_out);
  xor xor_2 (or_11_out[4], not_26_out, multiplexer_13_out_2[15]);
  Comparator #(.mode("unsigned"), .width(16)) comparator_1 (
    .a(multiplexer_7_out), .b(multiplexer_10_out), .gt(or_11_out[2]), .eq(or_11_out[3]));  // open: lt
  Adder #(.width(16)) adder_2 (
    .a(multiplexer_7_out), .b(multiplexer_10_out), .out(adder_2_out), .cout(adder_2_cout));  // open: cin
  Subtractor #(.width(16)) subtractor_1 (
    .a(multiplexer_7_out), .b(multiplexer_10_out), .out(subtractor_1_out), .bout(subtractor_1_bout));  // open: bin
  Multiplier #(.width(16)) multiplier_1 (
    .a(multiplexer_7_out), .b(multiplexer_10_out), .out(multiplier_1_out));  // open: cin, cout
  Divider #(.width(16)) divider_1 (
    .a(multiplexer_7_out), .b(multiplexer_10_out), .out(divider_1_out), .rem(divider_1_rem));  // open: upper
  assign and_20_out = multiplexer_7_out & multiplexer_10_out;  // AND_Gate and_20, 16 bits wide
  assign or_10_out = multiplexer_7_out | multiplexer_10_out;  // OR_Gate or_10, 16 bits wide
  Shifter #(.shift("rr"), .width(16)) shifter_1 (
    .in(multiplexer_7_out), .\dist (multiplexer_10_out[3:0]), .out(shifter_1_out));
  Shifter #(.width(16)) shifter_2 (.in(multiplexer_7_out), .\dist (multiplexer_10_out[3:0]), .out(shifter_2_out));
  Shifter #(.shift("lr"), .width(16)) shifter_3 (
    .in(multiplexer_7_out), .\dist (multiplexer_10_out[3:0]), .out(shifter_3_out));
  Shifter #(.shift("ar"), .width(16)) shifter_4 (
    .in(multiplexer_7_out), .\dist (multiplexer_10_out[3:0]), .out(shifter_4_out));
  or or_11 (or_11_out[0], subtractor_1_bout, adder_2_cout);
  Multiplexer #(.select(3), .width(16)) multiplexer_11 (
    .in0(adder_2_out), .in1(subtractor_1_out), .in2(multiplier_1_out), .in3(divider_1_out),
    .in4(divider_1_rem), .out(multiplexer_11_out), .sel(out_14[9:7]));  // open: in5, in6, in7
  Multiplexer #(.select(3), .width(16)) multiplexer_12 (
    .in0(and_20_out), .in1(or_10_out), .in4(shifter_1_out), .in5(shifter_2_out), .in6(shifter_3_out),
    .in7(shifter_4_out), .out(multiplexer_12_out), .sel(out_14[9:7]));  // open: in2, in3
  Multiplexer #(.width(16)) multiplexer_13 (
    .in0(multiplexer_11_out), .in1(multiplexer_12_out), .out({multiplexer_13_out_2[15], multiplexer_13_out}),
    .sel(and_2_out));
  assign controlled_buffer_1_out = and_19_out ? {multiplexer_13_out_2[15], multiplexer_13_out} : 16'bz;  // Controlled_Buffer controlled_buffer_4
  nand nand_2 (or_11_out[1], multiplexer_13_out[0], multiplexer_13_out[1], multiplexer_13_out[2], multiplexer_13_out[3], multiplexer_13_out[4], multiplexer_13_out[5], multiplexer_13_out[6], multiplexer_13_out[7], multiplexer_13_out[8], multiplexer_13_out[9], multiplexer_13_out[10], multiplexer_13_out[11], multiplexer_13_out[12], multiplexer_13_out[13], multiplexer_13_out[14], multiplexer_13_out_2[15]);
  Comparator #(.width(16)) comparator_2 (
    .a({multiplexer_9_out_2, multiplexer_9_out}), .b(16'h3ff), .eq(comparator_2_eq));  // open: gt, lt
  Comparator #(.width(16)) comparator_3 (
    .a({multiplexer_9_out_2, multiplexer_9_out}), .b(16'h3fe), .eq(comparator_3_eq));  // open: gt, lt
  nor nor_1 (nor_1_out, multiplexer_9_out[10], multiplexer_9_out[11], multiplexer_9_out_2[12], multiplexer_9_out_2[13], multiplexer_9_out_2[14], multiplexer_9_out_2[15]);
  and and_21 (and_21_out, multiplexer_9_out[5], multiplexer_9_out[6], multiplexer_9_out[7], multiplexer_9_out[8], multiplexer_9_out[9]);
  nor nor_2 (nor_2_out, multiplexer_9_out[10], multiplexer_9_out[11], multiplexer_9_out_2[12], multiplexer_9_out_2[13], multiplexer_9_out_2[14], multiplexer_9_out_2[15]);
  BitFinder #(.width(2)) bitfinder_1 (.in({1'b0, keyboard_1_avail[0]}), .index(bitfinder_1_index[0]));  // open: found
  Pull_Resistor pull_resistor_1 (.node(bitfinder_1_index[15]));
  nand nand_3 (nand_3_out, nor_1_out, and_22_out);
  and and_22 (and_22_out, and_21_out, nor_2_out);
  nor nor_3 (nor_3_out, multiplexer_9_out_2[12], multiplexer_9_out_2[13], multiplexer_9_out_2[14], multiplexer_9_out_2[15]);
  and and_23 (and_23_out, nor_1_out, nand_3_out);
  or or_12 (or_12_out, and_22_out, and_23_out);
  not not_27 (not_27_out, or_12_out);
  and and_24 (and_24_out, comparator_2_eq, and_10_out);
  assign controlled_buffer_5_out = comparator_3_eq ? {{15{bitfinder_1_index[15]}}, bitfinder_1_index[0]} : 16'bz;  // Controlled_Buffer controlled_buffer_5
  and and_25 (and_25_out, not_27_out, nor_3_out);
  not not_28 (not_28_out, out_14[0]);
  not not_29 (not_29_out, out_14[1]);
  not not_30 (not_30_out, out_14[3]);
  not not_31 (not_31_out, out_14[1]);
  not not_32 (not_32_out, out_14[3]);
  not not_33 (not_33_out, out_14[2]);
  not not_34 (not_34_out, out_14[3]);
  not not_35 (not_35_out, out_14[0]);
  not not_36 (not_36_out, out_14[2]);
  not not_37 (not_37_out, out_14[3]);
  not not_38 (not_38_out, out_14[1]);
  not not_39 (not_39_out, out_14[2]);
  not not_40 (not_40_out, out_14[3]);
  not not_41 (not_41_out, out_14[0]);
  not not_42 (not_42_out, out_14[1]);
  not not_43 (not_43_out, out_14[2]);
  not not_44 (not_44_out, out_14[3]);
  not not_45 (not_45_out, out_14[0]);
  not not_46 (not_46_out, out_14[3]);
  not not_47 (not_47_out, out_14[0]);
  not not_48 (not_48_out, out_14[0]);
  not not_49 (not_49_out, out_14[1]);
  not not_50 (not_50_out, out_14[2]);
  nor nor_4 (nor_4_out, and_22_out, and_23_out, and_25_out);
  or or_13 (or_13_out, and_24_out, and_41_out);
  and and_26 (and_26_out, not_28_out, not_29_out, out_14[2], not_30_out);
  LED led_1 (.in(and_26_out));
  and and_27 (and_27_out, out_14[0], not_31_out, out_14[2], not_32_out);
  LED led_2 (.in(and_27_out));
  and and_28 (and_28_out, out_14[0], out_14[1], not_33_out, not_34_out);
  LED led_3 (.in(and_28_out));
  and and_29 (and_29_out, not_35_out, out_14[1], not_36_out, not_37_out);
  LED led_4 (.in(and_29_out));
  and and_30 (and_30_out, out_14[0], not_38_out, not_39_out, not_40_out);
  LED led_5 (.in(and_30_out));
  and and_31 (and_31_out, not_41_out, not_42_out, not_43_out, not_44_out);
  LED led_6 (.in(and_31_out));
  and and_32 (and_32_out, not_45_out, out_14[1], out_14[2], not_46_out);
  LED led_7 (.in(and_32_out));
  and and_33 (and_33_out, not_47_out, out_14[1], out_14[2], out_14[3]);
  LED led_8 (.in(and_33_out));
  and and_34 (and_34_out, not_48_out, not_49_out, not_50_out, out_14[3]);
  LED led_9 (.in(and_34_out));
  or or_14 (or_14_out, and_10_out, or_6_out);
  T_Flip_Flop t_ff_1 (.T(or_13_out), .clk(Clock_0_out), .Q(t_ff_1_q), .reset(RESET_qn));  // open: Qn, preset
  assign controlled_buffer_6_out = or_15_out ? multiplexer_9_out[3:0] : 4'bz;  // Controlled_Buffer controlled_buffer_6
  or or_15 (or_15_out, and_35_out, and_22_out);
  and and_35 (and_35_out, and_22_out, or_6_out);
  not not_51 (not_51_out, t_ff_1_q);
  and and_36 (and_36_out, and_23_out, or_14_out);
  and and_37 (and_37_out, and_22_out, and_10_out);
  and and_38 (and_38_out, and_25_out, or_14_out);
  and and_39 (and_39_out, and_10_out, nor_4_out);
  and and_40 (and_40_out, or_6_out, nor_4_out);
  and and_41 (and_41_out, not_51_out, or_16_out);
  or or_16 (or_16_out, 1'b0, keyboard_1_avail[0]);
  Demultiplexer #(.select(4)) demultiplexer_2 (
    .out0(demultiplexer_2_out0), .out1(demultiplexer_2_out1), .in(1'b1), .sel(controlled_buffer_6_out));  // open: out2, out3, out4, out5, out6, out7, out8, out9, out10, out11, out12, out13, out14, out15
  and and_42 (and_42_out, demultiplexer_2_out1, and_35_out);
  or or_17 (or_17_out, and_39_out, and_40_out);
  Pull_Resistor pull_resistor_2 (.node(pull_resistor_2_node));
  and and_43 (and_43_out, or_17_out, Clock_0_out);
  TTY #(.cols(80), .rows(40)) tty_1 (
    .data(controlled_buffer_1_out[6:0]), .clk(Clock_0_out), .we(and_37_out), .clr(pull_resistor_2_node));
  Keyboard keyboard_1 (
    .clk(and_42_out), .re(and_42_out), .clr(pull_resistor_3_node), .avail(keyboard_1_avail[0]),
    .data(keyboard_1_data));
  Pull_Resistor pull_resistor_3 (.node(pull_resistor_3_node));
  ROM #(.addrWidth(10), .dataWidth(16)) SYSTEM (.addr(multiplexer_9_out[9:0]), .data(SYSTEM_data));
  Subtractor #(.width(12)) subtractor_2 (
    .a(multiplexer_9_out), .b(12'h400), .out(subtractor_2_out));  // open: bin, bout
  ROM #(.addrWidth(12), .dataWidth(16)) PROGRAM (.addr(subtractor_2_out), .data(PROGRAM_data));
  RAM #(.addrWidth(16), .clearpin("true"), .dataWidth(16), .\type ("nonvolatile")) MEMORY (
    .addr({multiplexer_9_out_2, multiplexer_9_out}), .we(and_39_out), .oe(and_40_out), .clk(and_43_out),
    .din(controlled_buffer_1_out), .dout(MEMORY_dout), .clr(RESET_qn));
  assign controlled_buffer_7_out = pull_resistor_4_node ? {{9{1'b0}}, keyboard_1_data} : 16'bz;  // Controlled_Buffer controlled_buffer_7
  Pull_Resistor pull_resistor_4 (.node(pull_resistor_4_node));
  assign controlled_buffer_1_out = and_36_out ? SYSTEM_data : 16'bz;  // Controlled_Buffer controlled_buffer_8
  assign controlled_buffer_1_out = and_38_out ? PROGRAM_data : 16'bz;  // Controlled_Buffer controlled_buffer_9
  assign controlled_buffer_1_out = and_40_out ? MEMORY_dout : 16'bz;  // Controlled_Buffer controlled_buffer_10

  assign out_3 = out_1;
  assign out_4 = out_2;
  assign out_7 = out_5;
  assign out_8 = out_6;
  assign out_11 = out_9;
  assign out_12 = out_10;
  assign out_15 = out_13;
  assign out_16 = out_14;
  assign out_18 = out_17;

  // Other names for the same wires on the sheet: IR[15:0] = out_14; PC[15:0] = out_10; R0[15:0] = out_1;
  //   R1[15:0] = out_5; R2[15:0] = out_9; R3[15:0] = out_13; R4[15:0] = out_17; R5[15:0] = out_2; SP[15:0] = out_6

  // Notes on the sheet:
  //   Clock
  //   Read Instruction
  //   Reset
  //   Reset
  //   Set Flags
  //   0100 ARITHMETIC
  //   0101 LOGICAL
  //   0011 STOR
  //   0010 MOV IMM
  //   0001 LOAD
  //   0110 LOAD NEXT
  //   0000 MOV
  //   0111 INC
  //   1000 DEC
  //   Look Ahead
  //   Read Instruction
  //   Output Immediate
  //   Output A
  //   Output B
  //   Immediate to B
  //   Logical/Shift
  //   ALU Out
  //   Write Memory
  //   Read Memory
  //   Arguments
  //   Flags
  //   Data Bus
  //   Register Write
  //   Reset
  //   Arguments
  //   Clock
  //   Reset
  //   Clock
  //   Interrupt
  //   Interrupt
  //   Look Ahead
  //   Read Instruction
  //   Output Immediate
  //   Output A
  //   Output B
  //   Immediate to B
  //   Arith or Logical/Shift
  //   ALU Out
  //   Write Memory
  //   Read Memory
  //   Arguments
  //   Write Memory
  //   Read Memory
  //   Interrupt
  //   Reset
  //   Address Bus
  //   Data Bus
  //   Interrupt
  //   Reset
  //   Clock
  //   Write Memory
  //   Read Memory
  //   Done Interrupt
  //   Read Interrupt Vector
  //   SYSROM 0-1023 (0x0-0x3FF)
  //   BUS 992-1023 (0x3EF-0x3FF)
  //   PROGRAM 1024-4095 (0x100-0xFFF)
  //   RAM 4096-65535 (0x0-0xFFFF)
  //   0100 ARITHMETIC
  //   0101 LOGICAL
  //   0011 STOR
  //   0010 MOV IMM
  //   0001 LOAD
  //   0000 MOV
  //   0110 LOAD NEXT
  //   0111 INC
  //   1000 DEC
  //   Interrupt
  //   Ram Write
  //   Ram Read
  //   Interrupt
  //   Write
  //   Read
  //   Write
  //   Read
  //   Interrupt
  //   Data Bus
  //   Address Bus
  //   Rom Enable
  //   contents of SYSTEM (hex, n*v repeats v):
  //   76 400
  //   contents of PROGRAM (hex, n*v repeats v):
  //   82 112 1a2 232 2c2 352 3e2 76 400
endmodule

module test (
  input  [15:0] in_1,
  input  in_2
);
endmodule
