// Logisim project computer_beta2.circ as structural Verilog: 2 circuits, main circuit ComputerNew
module ComputerNew (
  input  in_1,
  output [15:0] out_2,
  output [15:0] out_3,
  output [3:0] BUSIDSelect,
  output BUSWrite
);

  wire adder_3_cout, and_1_out, and_2_out, and_3_out, and_4_out, and_5_out, and_6_out, and_7_out, and_8_out,
       and_9_out, and_10_out, and_11_out, and_12_out, and_13_out, and_14_out, and_15_out, and_16_out,
       and_17_out, and_18_out, and_20_out, and_21_out, and_22_out, and_23_out, and_24_out, and_25_out,
       and_26_out, and_27_out, Clock_0_out, demultiplexer_1_out0, demultiplexer_1_out1, demultiplexer_1_out2,
       demultiplexer_1_out3, demultiplexer_1_out4, demultiplexer_1_out5, demultiplexer_1_out6,
       demultiplexer_1_out7, keyboard_1_avail, multiplexer_2_out, nand_1_out, nand_3_out, nor_1_out,
       nor_2_out, nor_3_out, nor_4_out, not_1_out, not_2_out, not_3_out, not_4_out, not_5_out, not_6_out,
       not_7_out, not_8_out, not_9_out, not_10_out, not_11_out, not_12_out, not_13_out, not_14_out,
       not_15_out, not_16_out, not_17_out, not_18_out, not_19_out, not_20_out, not_21_out, not_22_out,
       not_23_out, not_24_out, not_25_out, not_26_out, or_1_out, or_2_out, or_3_out, or_4_out, or_5_out,
       or_6_out, or_7_out, or_8_out, or_9_out, or_12_out, or_13_out, or_14_out, pull_resistor_1_node,
       pull_resistor_2_node, pull_resistor_3_node, RESET_qn, subtractor_1_bout, xor_1_out;
  wire [2:0] multiplexer_7_out;
  wire [4:0] FLAGS_q, or_11_out;
  wire [6:0] keyboard_1_data;
  wire [11:0] multiplexer_10_out, subtractor_2_out;
  wire [14:0] multiplexer_14_out;
  wire [15:0] adder_1_out, adder_2_out, adder_3_out, and_19_out, controlled_buffer_4_out, divider_1_out,
       divider_1_rem, IR_q, MEMORY_dout, multiplexer_1_out, multiplexer_3_out, multiplexer_4_out,
       multiplexer_5_out, multiplexer_6_out, multiplexer_8_out, multiplexer_9_out, multiplexer_11_out,
       multiplexer_12_out, multiplexer_13_out, multiplier_1_out, or_10_out, PROGRAM_data, R0_q, R1_q, R2_q,
       R3_q, R4_q, R5_q, shifter_1_out, shifter_2_out, shifter_3_out, shifter_4_out, SP_q, subtractor_1_out,
       SYSTEM_data;
  wire [15:12] multiplexer_10_out_2;
  wire [15:15] multiplexer_14_out_2;

  Clock Clock_0 (.out(Clock_0_out));
  not not_1 (not_1_out, Clock_0_out);
  J_K_Flip_Flop #(.trigger("falling")) RESET (
    .J(1'b1), .K(1'b0), .clk(Clock_0_out), .Qn(RESET_qn));  // open: Q, preset, reset
  Register #(.width(5)) FLAGS (.D(or_11_out), .en(or_1_out), .clk(Clock_0_out), .Q(FLAGS_q), .clr(RESET_qn));
  Register #(.trigger("low"), .width(16)) IR (.D(out_2), .en(not_1_out), .clk(Clock_0_out), .Q(IR_q), .clr(RESET_qn));
  Multiplexer #(.enable("false"), .width(16)) multiplexer_1 (
    .in0(IR_q), .in1(16'he00f), .out(multiplexer_1_out), .sel(keyboard_1_avail));
  Multiplexer #(.enable("false"), .select(3)) multiplexer_2 (
    .in0(1'b1), .in1(FLAGS_q[0]), .in2(FLAGS_q[1]), .in3(FLAGS_q[2]), .in4(FLAGS_q[3]), .in5(FLAGS_q[4]),
    .in6(1'b1), .in7(1'b1), .out(multiplexer_2_out), .sel(multiplexer_1_out[9:7]));
  not not_2 (not_2_out, multiplexer_1_out[0]);
  not not_3 (not_3_out, multiplexer_1_out[1]);
  not not_4 (not_4_out, multiplexer_1_out[3]);
  not not_5 (not_5_out, multiplexer_1_out[1]);
  not not_6 (not_6_out, multiplexer_1_out[3]);
  not not_7 (not_7_out, multiplexer_1_out[2]);
  not not_8 (not_8_out, multiplexer_1_out[3]);
  not not_9 (not_9_out, multiplexer_1_out[0]);
  not not_10 (not_10_out, multiplexer_1_out[2]);
  not not_11 (not_11_out, multiplexer_1_out[3]);
  not not_12 (not_12_out, multiplexer_1_out[1]);
  not not_13 (not_13_out, multiplexer_1_out[2]);
  not not_14 (not_14_out, multiplexer_1_out[3]);
  not not_15 (not_15_out, multiplexer_1_out[0]);
  not not_16 (not_16_out, multiplexer_1_out[1]);
  not not_17 (not_17_out, multiplexer_1_out[2]);
  not not_18 (not_18_out, multiplexer_1_out[3]);
  not not_19 (not_19_out, multiplexer_1_out[0]);
  not not_20 (not_20_out, multiplexer_1_out[3]);
  not not_21 (not_21_out, multiplexer_1_out[0]);
  not not_22 (not_22_out, multiplexer_1_out[0]);
  not not_23 (not_23_out, multiplexer_1_out[1]);
  not not_24 (not_24_out, multiplexer_1_out[2]);
  and and_1 (and_1_out, not_2_out, not_3_out, multiplexer_1_out[2], not_4_out);
  and and_2 (and_2_out, multiplexer_1_out[0], not_5_out, multiplexer_1_out[2], not_6_out);
  and and_3 (and_3_out, multiplexer_1_out[0], multiplexer_1_out[1], not_7_out, not_8_out);
  and and_4 (and_4_out, not_9_out, multiplexer_1_out[1], not_10_out, not_11_out);
  and and_5 (and_5_out, multiplexer_1_out[0], not_12_out, not_13_out, not_14_out);
  and and_6 (and_6_out, not_15_out, not_16_out, not_17_out, not_18_out);
  and and_7 (and_7_out, not_19_out, multiplexer_1_out[1], multiplexer_1_out[2], not_20_out);
  and and_8 (and_8_out, not_21_out, multiplexer_1_out[1], multiplexer_1_out[2], multiplexer_1_out[3]);
  and and_9 (and_9_out, not_22_out, not_23_out, not_24_out, multiplexer_1_out[3]);
  or or_1 (or_1_out, and_1_out, and_2_out);
  and and_10 (and_10_out, and_3_out, multiplexer_2_out);
  and and_11 (and_11_out, and_5_out, multiplexer_2_out);
  and and_12 (and_12_out, and_6_out, multiplexer_2_out);
  and and_13 (and_13_out, and_7_out, multiplexer_2_out);
  or or_2 (or_2_out, and_9_out, and_8_out);
  or or_3 (or_3_out, and_13_out, and_1_out, and_2_out, and_8_out, and_9_out, and_4_out, and_11_out, and_12_out);
  or or_4 (or_4_out, and_2_out, or_2_out, and_1_out);
  or or_5 (or_5_out, and_13_out, and_11_out);
  or or_6 (or_6_out, or_5_out, not_1_out);
  Demultiplexer #(.enable("false"), .select(3)) demultiplexer_1 (
    .out0(demultiplexer_1_out0), .out1(demultiplexer_1_out1), .out2(demultiplexer_1_out2),
    .out3(demultiplexer_1_out3), .out4(demultiplexer_1_out4), .out5(demultiplexer_1_out5),
    .out6(demultiplexer_1_out6), .out7(demultiplexer_1_out7), .in(or_3_out), .sel(multiplexer_1_out[6:4]));
  Register #(.trigger("falling"), .width(16)) R0 (
    .D(out_2), .en(demultiplexer_1_out0), .clk(Clock_0_out), .Q(R0_q), .clr(Clock_0_out));
  Register #(.trigger("falling"), .width(16)) R4 (
    .D(out_2), .en(demultiplexer_1_out4), .clk(Clock_0_out), .Q(R4_q), .clr(Clock_0_out));
  Register #(.trigger("falling"), .width(16)) R1 (
    .D(out_2), .en(demultiplexer_1_out1), .clk(Clock_0_out), .Q(R1_q), .clr(Clock_0_out));
  Register #(.trigger("falling"), .width(16)) R5 (
    .D(out_2), .en(demultiplexer_1_out5), .clk(Clock_0_out), .Q(R5_q), .clr(Clock_0_out));
  Register #(.trigger("falling"), .width(16)) R2 (
    .D(out_2), .en(demultiplexer_1_out2), .clk(Clock_0_out), .Q(R2_q), .clr(Clock_0_out));
  Register #(.trigger("falling"), .width(16)) SP (
    .D(out_2), .en(demultiplexer_1_out6), .clk(Clock_0_out), .Q(SP_q), .clr(Clock_0_out));
  Register #(.trigger("falling"), .width(16)) R3 (
    .D(out_2), .en(demultiplexer_1_out3), .clk(Clock_0_out), .Q(R3_q), .clr(Clock_0_out));
  Multiplexer #(.enable("false"), .width(16)) multiplexer_3 (
    .in0(adder_2_out), .in1(out_2), .out(multiplexer_3_out), .sel(demultiplexer_1_out7));
  or or_7 (or_7_out, demultiplexer_1_out7, Clock_0_out);
  Register #(.trigger("falling"), .width(16)) PC (
    .D(multiplexer_3_out), .en(nand_1_out), .clk(Clock_0_out), .Q(out_3), .clr(Clock_0_out));
  nand nand_1 (nand_1_out, or_7_out, keyboard_1_avail);
  Multiplexer #(.enable("false"), .width(16)) multiplexer_4 (
    .in0(16'h1), .in1(16'h2), .out(multiplexer_4_out), .sel(and_13_out));
  Adder #(.width(16)) adder_1 (.a(out_3), .b(16'h1), .out(adder_1_out));  // open: cin, cout
  Adder #(.width(16)) adder_2 (.a(out_3), .b(multiplexer_4_out), .out(adder_2_out));  // open: cin, cout
  and and_14 (and_14_out, Clock_0_out, and_13_out);
  Multiplexer #(.enable("false"), .width(16)) multiplexer_5 (
    .in0(out_3), .in1(adder_1_out), .out(multiplexer_5_out), .sel(and_14_out));
  Multiplexer #(.enable("false"), .width(16)) multiplexer_6 (
    .in0(multiplexer_5_out), .in1(16'h1), .out(multiplexer_6_out), .sel(keyboard_1_avail));
  or or_8 (or_8_out, and_13_out, not_1_out);
  Multiplexer #(.enable("false"), .width(3)) multiplexer_7 (
    .in0(multiplexer_1_out[15:13]), .in1(3'b111), .out(multiplexer_7_out), .sel(or_8_out));
  Multiplexer #(.enable("false"), .select(3), .width(16)) multiplexer_8 (
    .in0(R0_q), .in1(R1_q), .in2(R2_q), .in3(R3_q), .in4(R4_q), .in5(R5_q), .in6(SP_q),
    .in7(multiplexer_6_out), .out(multiplexer_8_out), .sel(multiplexer_1_out[12:10]));
  Multiplexer #(.enable("false"), .select(3), .width(16)) multiplexer_9 (
    .in0(R0_q), .in1(R1_q), .in2(R2_q), .in3(R3_q), .in4(R4_q), .in5(R5_q), .in6(SP_q),
    .in7(multiplexer_6_out), .out(multiplexer_9_out), .sel(multiplexer_7_out));
  Multiplexer #(.enable("false"), .select(3), .width(16)) multiplexer_10 (
    .in0(R0_q), .in1(R1_q), .in2(R2_q), .in3(R3_q), .in4(R4_q), .in5(R5_q), .in6(SP_q),
    .in7(multiplexer_6_out), .out({multiplexer_10_out_2, multiplexer_10_out}), .sel(multiplexer_7_out));
  assign out_2 = and_15_out ? multiplexer_8_out : 16'bz;  // Controlled_Buffer controlled_buffer_1
  and and_15 (and_15_out, Clock_0_out, and_10_out);
  assign out_2 = and_16_out ? multiplexer_9_out : 16'bz;  // Controlled_Buffer controlled_buffer_2
  and and_16 (and_16_out, Clock_0_out, and_12_out);
  and and_17 (and_17_out, Clock_0_out, and_4_out);
  assign out_2 = and_17_out ? {{7{1'b0}}, multiplexer_1_out[15:7]} : 16'bz;  // Controlled_Buffer controlled_buffer_3
  and and_18 (and_18_out, Clock_0_out, or_9_out);
  or or_9 (or_9_out, and_2_out, or_4_out);
  Multiplexer #(.enable("false"), .width(16)) multiplexer_11 (
    .in0(multiplexer_9_out), .in1({{7{1'b0}}, multiplexer_1_out[15:7]}), .out(multiplexer_11_out),
    .sel(or_2_out));
  xor xor_1 (xor_1_out, multiplexer_11_out[15], multiplexer_8_out[15]);
  not not_25 (not_25_out, xor_1_out);
  xor xor_2 (or_11_out[4], not_25_out, multiplexer_14_out_2[15]);
  Comparator #(.mode("unsigned"), .width(16)) comparator_1 (
    .a(multiplexer_8_out), .b(multiplexer_11_out), .gt(or_11_out[2]), .eq(or_11_out[3]));  // open: lt
  Adder #(.width(16)) adder_3 (
    .a(multiplexer_8_out), .b(multiplexer_11_out), .out(adder_3_out), .cout(adder_3_cout));  // open: cin
  Subtractor #(.width(16)) subtractor_1 (
    .a(multiplexer_8_out), .b(multiplexer_11_out), .out(subtractor_1_out), .bout(subtractor_1_bout));  // open: bin
  Multiplier #(.width(16)) multiplier_1 (
    .a(multiplexer_8_out), .b(multiplexer_11_out), .out(multiplier_1_out));  // open: cin, cout
  Divider #(.width(16)) divider_1 (
    .a(multiplexer_8_out), .b(multiplexer_11_out), .out(divider_1_out), .rem(divider_1_rem));  // open: upper
  assign and_19_out = multiplexer_8_out & multiplexer_11_out;  // AND_Gate and_19, 16 bits wide
  assign or_10_out = multiplexer_8_out | multiplexer_11_out;  // OR_Gate or_10, 16 bits wide
  Shifter #(.shift("rr"), .width(16)) shifter_1 (
    .in(multiplexer_8_out), .\dist (multiplexer_11_out[3:0]), .out(shifter_1_out));
  Shifter #(.width(16)) shifter_2 (.in(multiplexer_8_out), .\dist (multiplexer_11_out[3:0]), .out(shifter_2_out));
  Shifter #(.shift("lr"), .width(16)) shifter_3 (
    .in(multiplexer_8_out), .\dist (multiplexer_11_out[3:0]), .out(shifter_3_out));
  Shifter #(.shift("ar"), .width(16)) shifter_4 (
    .in(multiplexer_8_out), .\dist (multiplexer_11_out[3:0]), .out(shifter_4_out));
  or or_11 (or_11_out[0], subtractor_1_bout, adder_3_cout);
  Pull_Resistor #(.pull(1)) pull_resistor_1 (.node(pull_resistor_1_node));
  Keyboard keyboard_1 (
    .clk(Clock_0_out), .re(pull_resistor_1_node), .clr(pull_resistor_2_node), .avail(keyboard_1_avail),
    .data(keyboard_1_data));
  Pull_Resistor pull_resistor_2 (.node(pull_resistor_2_node));
  Multiplexer #(.enable("false"), .select(3), .width(16)) multiplexer_12 (
    .in0(adder_3_out), .in1(subtractor_1_out), .in2(multiplier_1_out), .in3(divider_1_out),
    .in4(divider_1_rem), .out(multiplexer_12_out), .sel(multiplexer_1_out[9:7]));  // open: in5, in6, in7
  Multiplexer #(.enable("false"), .select(3), .width(16)) multiplexer_13 (
    .in0(and_19_out), .in1(or_10_out), .in4(shifter_1_out), .in5(shifter_2_out), .in6(shifter_3_out),
    .in7(shifter_4_out), .out(multiplexer_13_out), .sel(multiplexer_1_out[9:7]));  // open: in2, in3
  Multiplexer #(.enable("false"), .width(16)) multiplexer_14 (
    .in0(multiplexer_12_out), .in1(multiplexer_13_out), .out({multiplexer_14_out_2[15], multiplexer_14_out}),
    .sel(and_2_out));
  assign controlled_buffer_4_out = pull_resistor_3_node ? {{9{1'b0}}, keyboard_1_data} : 16'bz;  // Controlled_Buffer controlled_buffer_4
  assign out_2 = and_18_out ? {multiplexer_14_out_2[15], multiplexer_14_out} : 16'bz;  // Controlled_Buffer controlled_buffer_5
  nand nand_2 (or_11_out[1], multiplexer_14_out[0], multiplexer_14_out[1], multiplexer_14_out[2], multiplexer_14_out[3], multiplexer_14_out[4], multiplexer_14_out[5], multiplexer_14_out[6], multiplexer_14_out[7], multiplexer_14_out[8], multiplexer_14_out[9], multiplexer_14_out[10], multiplexer_14_out[11], multiplexer_14_out[12], multiplexer_14_out[13], multiplexer_14_out[14], multiplexer_14_out_2[15]);
  Pull_Resistor pull_resistor_3 (.node(pull_resistor_3_node));
  nor nor_1 (nor_1_out, multiplexer_10_out[10], multiplexer_10_out[11], multiplexer_10_out_2[12], multiplexer_10_out_2[13], multiplexer_10_out_2[14], multiplexer_10_out_2[15]);
  and and_20 (and_20_out, multiplexer_10_out[5], multiplexer_10_out[6], multiplexer_10_out[7], multiplexer_10_out[8], multiplexer_10_out[9]);
  nor nor_2 (nor_2_out, multiplexer_10_out[10], multiplexer_10_out[11], multiplexer_10_out_2[12], multiplexer_10_out_2[13], multiplexer_10_out_2[14], multiplexer_10_out_2[15]);
  and and_21 (and_21_out, and_20_out, nor_2_out);
  nor nor_3 (nor_3_out, multiplexer_10_out_2[12], multiplexer_10_out_2[13], multiplexer_10_out_2[14], multiplexer_10_out_2[15]);
  nand nand_3 (nand_3_out, nor_1_out, and_21_out);
  and and_22 (and_22_out, nor_1_out, nand_3_out);
  or or_12 (or_12_out, and_21_out, and_22_out);
  not not_26 (not_26_out, or_12_out);
  and and_23 (and_23_out, not_26_out, nor_3_out);
  nor nor_4 (nor_4_out, and_21_out, and_22_out, and_23_out);
  or or_13 (or_13_out, and_10_out, or_6_out);
  and and_24 (and_24_out, and_22_out, or_13_out);
  assign BUSIDSelect = and_21_out ? multiplexer_10_out[3:0] : 4'bz;  // Controlled_Buffer controlled_buffer_6
  and and_25 (and_25_out, and_10_out, nor_4_out);
  and and_26 (and_26_out, or_6_out, nor_4_out);
  and and_27 (and_27_out, and_23_out, or_13_out);
  and and_28 (BUSWrite, and_21_out, and_10_out);
  or or_14 (or_14_out, and_26_out, RESET_qn);
  ROM #(.addrWidth(10), .dataWidth(16)) SYSTEM (.addr(multiplexer_10_out[9:0]), .data(SYSTEM_data));
  Subtractor #(.width(12)) subtractor_2 (
    .a(multiplexer_10_out), .b(12'h400), .out(subtractor_2_out));  // open: bin, bout
  ROM #(.addrWidth(12), .dataWidth(16)) PROGRAM (.addr(subtractor_2_out), .data(PROGRAM_data));
  RAM #(.addrWidth(16), .dataWidth(16), .readbehav("war"), .\type ("nonvolatile")) MEMORY (
    .addr({multiplexer_10_out_2, multiplexer_10_out}), .we(and_25_out), .oe(in_1), .clk(Clock_0_out),
    .din(out_2), .dout(MEMORY_dout));
  assign out_2 = and_24_out ? SYSTEM_data : 16'bz;  // Controlled_Buffer controlled_buffer_7
  assign out_2 = and_27_out ? PROGRAM_data : 16'bz;  // Controlled_Buffer controlled_buffer_8
  assign out_2 = or_14_out ? MEMORY_dout : 16'bz;  // Controlled_Buffer controlled_buffer_9

  // Notes on the sheet:
  //   Clock
  //   Read Instruction
  //   Reset
  //   Reset
  //   Interrupt
  //   Set Flags
  //   0100 ARITHMETIC
  //   0101 LOGICAL
  //   0011 STOR
  //   0010 MOV IMM
  //   0001 LOAD
  //   0110 LOAD NEXT
  //   0000 MOV
  //   0111 INC
  //   1000 DEC
  //   Look Ahead
  //   Read Instruction
  //   Output Immediate
  //   Output A
  //   Output B
  //   Immediate to B
  //   Logical/Shift
  //   ALU Out
  //   Write Memory
  //   Read Memory
  //   Arguments
  //   Interrupt
  //   Flags
  //   Data Bus
  //   Register Write
  //   Reset
  //   Arguments
  //   Clock
  //   Reset
  //   Clock
  //   Interrupt
  //   Interrupt
  //   Look Ahead
  //   Read Instruction
  //   Output Immediate
  //   Output B
  //   Immediate to B
  //   Arith or Logical/Shift
  //   ALU Out
  //   Write Memory
  //   Read Memory
  //   Arguments
  //   Read Instruction
  //   Reset
  //   Write Memory
  //   Read Memory
  //   Interrupt
  //   Register Address Bus
  //   Clock
  //   Data Bus
  //   Interrupt
  //   Write Memory
  //   Read Memory
  //   Interrupt
  //   SYSROM 0-1023 (0x0-0x3FF)
  //   BUS 992-1023 (0x3EF-0x3FF)
  //   PROGRAM 1024-4095 (0x100-0xFFF)
  //   RAM 4096-65535 (0x0-0xFFFF)
  //   Data Bus
  //   Address Bus
  //   Rom Enable
  //   Ram Write
  //   Ram Read
  //   contents of SYSTEM (hex, n*v repeats v):
  //   76 400
  //   contents of PROGRAM (hex, n*v repeats v):
  //   82 112 2004 92 2285 36 1000 6003 6041 76 400
endmodule

module test (
  input  [15:0] in_1,
  input  in_2,
  input  in_3
);

  wire clock_1_out;
  wire [15:0] MEMORY_dout;

  Clock clock_1 (.out(clock_1_out));
  RAM #(.addrWidth(16), .dataWidth(16), .readbehav("war"), .\type ("nonvolatile")) MEMORY (
    .addr(16'h1), .we(in_2), .oe(in_3), .clk(clock_1_out), .din(MEMORY_dout), .dout(MEMORY_dout));
endmodule
